// Logisim project flipflops.circ as structural Verilog: 1 circuit, main circuit main
module main (
  input  R,
  input  S,
  input  S_2,
  input  R_2,
  input  K,
  input  J
);

  wire and_1_out, and_2_out, and_3_out, and_4_out, button_1_out, button_2_out, nor_1_out, nor_2_out,
       nor_3_out, nor_4_out, nor_5_out, nor_6_out;

  Button button_1 (.out(button_1_out));
  Button button_2 (.out(button_2_out));
  and and_1 (and_1_out, R, button_1_out);
  and and_2 (and_2_out, button_1_out, S);
  nor nor_1 (nor_1_out, S_2, nor_2_out);
  nor nor_2 (nor_2_out, nor_1_out, R_2);
  and and_3 (and_3_out, nor_6_out, K, button_2_out);
  and and_4 (and_4_out, button_2_out, J, nor_4_out);
  nor nor_3 (nor_3_out, nor_5_out, and_2_out);
  nor nor_4 (nor_4_out, nor_6_out, and_4_out);
  nor nor_5 (nor_5_out, and_1_out, nor_3_out);
  nor nor_6 (nor_6_out, and_3_out, nor_4_out);
  LED led_1 (.in(nor_1_out));
  LED led_2 (.in(nor_2_out));
  LED led_3 (.in(nor_6_out));
  LED led_4 (.in(nor_4_out));

  // Notes on the sheet:
  //   CLOCK
  //   CLOCK
  //   Q
  //   Q'
  //   Q
  //   Q'
  //   Q
  //   Q'
endmodule
