// Logisim project somador4bits.circ as structural Verilog: 1 circuit, main circuit main
module main (
  input  Cin,
  input  in_2,
  input  in_3,
  input  in_4,
  input  in_5,
  input  in_6,
  input  in_7,
  input  in_8,
  input  PSW
);

  wire and_1_out, and_2_out, and_3_out, and_4_out, and_5_out, and_6_out, and_7_out, and_8_out, and_9_out,
       and_10_out, and_11_out, and_12_out, and_13_out, and_14_out, and_15_out, and_16_out, and_17_out,
       and_18_out, and_19_out, and_20_out, and_21_out, and_22_out, and_23_out, and_24_out, and_25_out,
       and_26_out, and_27_out, and_28_out, and_29_out, and_30_out, and_31_out, and_32_out, not_1_out,
       not_2_out, not_3_out, not_4_out, not_5_out, not_6_out, not_7_out, not_8_out, not_9_out, not_10_out,
       not_11_out, not_12_out, or_1_out, or_2_out, or_3_out, or_4_out, or_5_out, or_6_out, or_7_out, or_8_out;

  and and_1 (and_1_out, not_3_out, not_1_out, in_2);
  not not_1 (not_1_out, in_3);
  not not_2 (not_2_out, in_2);
  not not_3 (not_3_out, Cin);
  and and_2 (and_2_out, not_3_out, in_3, not_2_out);
  or or_1 (or_1_out, and_1_out, and_2_out, and_4_out, and_3_out);
  and and_3 (and_3_out, Cin, in_2, in_3);
  and and_4 (and_4_out, Cin, not_1_out, not_2_out);
  and and_5 (and_5_out, not_3_out, in_3, in_2);
  Adder adder_1 ();  // open: a, b, out, cin, cout
  and and_6 (and_6_out, Cin, not_1_out, in_2);
  LED led_1 (.in(or_6_out));
  LED led_2 (.in(or_8_out));
  and and_7 (and_7_out, Cin, in_3, not_2_out);
  or or_2 (or_2_out, and_5_out, and_6_out, and_7_out, and_8_out);
  LED led_3 (.in(or_2_out));
  LED led_4 (.in(or_5_out));
  and and_8 (and_8_out, Cin, in_2, in_3);
  LED led_5 (.in(or_3_out));
  LED led_6 (.in(or_1_out));
  and and_9 (and_9_out, not_6_out, not_4_out, in_5);
  not not_4 (not_4_out, in_4);
  not not_5 (not_5_out, in_5);
  not not_6 (not_6_out, or_2_out);
  and and_10 (and_10_out, not_6_out, in_4, not_5_out);
  and and_11 (and_11_out, or_2_out, not_4_out, not_5_out);
  or or_3 (or_3_out, and_9_out, and_10_out, and_11_out, and_12_out);
  and and_12 (and_12_out, or_2_out, in_5, in_4);
  and and_13 (and_13_out, not_6_out, in_4, in_5);
  and and_14 (and_14_out, or_2_out, not_4_out, in_5);
  or or_4 (or_4_out, and_13_out, and_14_out, and_15_out, and_16_out);
  LED led_7 (.in(or_4_out));
  and and_15 (and_15_out, or_2_out, in_4, not_5_out);
  and and_16 (and_16_out, or_2_out, in_5, in_4);
  and and_17 (and_17_out, not_9_out, not_7_out, in_7);
  and and_18 (and_18_out, not_12_out, not_10_out, PSW);
  not not_7 (not_7_out, in_6);
  not not_8 (not_8_out, in_7);
  not not_9 (not_9_out, or_4_out);
  and and_19 (and_19_out, not_9_out, in_6, not_8_out);
  or or_5 (or_5_out, and_17_out, and_19_out, and_22_out, and_21_out);
  not not_10 (not_10_out, in_8);
  not not_11 (not_11_out, PSW);
  not not_12 (not_12_out, or_7_out);
  and and_20 (and_20_out, not_12_out, in_8, not_11_out);
  or or_6 (or_6_out, and_18_out, and_20_out, and_23_out, and_25_out);
  and and_21 (and_21_out, or_4_out, in_7, in_6);
  and and_22 (and_22_out, or_4_out, not_7_out, not_8_out);
  and and_23 (and_23_out, or_7_out, not_10_out, not_11_out);
  and and_24 (and_24_out, not_9_out, in_6, in_7);
  and and_25 (and_25_out, or_7_out, PSW, in_8);
  and and_26 (and_26_out, not_12_out, in_8, PSW);
  and and_27 (and_27_out, or_4_out, not_7_out, in_7);
  and and_28 (and_28_out, or_7_out, not_10_out, PSW);
  and and_29 (and_29_out, or_4_out, in_6, not_8_out);
  or or_7 (or_7_out, and_24_out, and_27_out, and_29_out, and_31_out);
  LED led_8 (.in(or_7_out));
  and and_30 (and_30_out, or_7_out, in_8, not_11_out);
  or or_8 (or_8_out, and_26_out, and_28_out, and_30_out, and_32_out);
  and and_31 (and_31_out, or_4_out, in_7, in_6);
  and and_32 (and_32_out, or_7_out, PSW, in_8);

  // Notes on the sheet:
  //   A
  //   B
  //   A
  //   B
  //   Cin
  //   A
  //   B
  //   Cin
  //   A
  //   B
  //   Cin
endmodule
